# Fritzing sketch fingerPrintLockSchem (saved by Fritzing 0.9.9b)

parts:
  Part2 = Bluetooth HC-05 Macho
  R3 = Resistor [tolerance=±5% resistance=220 package="0805 [SMD]"]
  R4 = Resistor [tolerance=±5% resistance=220 package="0805 [SMD]"]
  R2 = Resistor [tolerance=±5% resistance=1.2k package="1206 [SMD]"]
  Part3 = Arduino Nano (Rev3.0) (ICSP)
  M1_-_USB-C = TP4056 Module [part_number=HW-107]
  M2_-_5V_Output = MT3608 Module
  BAT1 = 18650 battery holder [package=battery-18650-kit]
  BAT2 = 18650 battery holder [package=battery-18650-kit]
  U1 = LCD-16X2 [package=lcd-16x2_nosilk]
  LCM1602_IIC1 = LCM1602 IIC [part_number="LCM1602 IIC" chip_label="LCM1602 IIC" package="DIP (Dual Inline) [THT]"]
  S2 = SPST Switch [package=switch-spdt]
  S1 = Momentary Switch [package=ksa_sealed_tac_switch]
  LED2 = Super Flux RGB LED (com. cathode) [color=Blue]
  S3 = Magnetic Door Switch [package=reed_switch_plastic]
  Adafruit_Z70 = sensor_biometrico
  J1 = Basic Servo

nets:
  N1: Part2.State, Part3.D7
  N2: Part2.TXD, Part3.D8
  N3: Part2.RXD, Part3.D9
  VCC: Part2.VCC, Part3.3V3
  GND: Part2.GND, R2.Pin_0, Part3.GND, M2_-_5V_Output.pin4, LED2.common_cathode, S3.1, Adafruit_Z70.GND, J1.gnd
  N4: R3.Pin_0, Part3.D13/SCK
  N5: R3.Pin_1, LED2.red_anode
  N6: R4.Pin_0, Part3.D12/MISO
  N7: R4.Pin_1, LED2.green_anode
  N8: R2.Pin_1, S1.3
  N9: Part3.RESET, Part3.D3
  N10: Part3.D4, Adafruit_Z70.RX
  N11: Part3.D5, Adafruit_Z70.TX
  N12: Part3.D6, S1.4
  N13: Part3.D10, J1.pulse
  N14: Part3.D11/MOSI, S3.2
  N15: Part3.VIN, M2_-_5V_Output.pin3
  VCC_2: Part3.5V, LCM1602_IIC1.VCC, S1.1, Adafruit_Z70.VCC, J1.vcc
  N16: Part3.A5, LCM1602_IIC1.SCL
  N17: Part3.A4, LCM1602_IIC1.SDA
  N18: M1_-_USB-C.OUT-#1, M2_-_5V_Output.pin1
  N19: M1_-_USB-C.BAT-, BAT1.-, BAT2.-
  N20: M1_-_USB-C.BAT+, BAT1.+, BAT2.+
  N21: M1_-_USB-C.OUT-#4, S2.S
  N22: M2_-_5V_Output.pin2, S2.O
  VSS: U1.VSS, LCM1602_IIC1.VSS
  VDD: U1.VDD, LCM1602_IIC1.VDD
  N23: U1.VO, LCM1602_IIC1.V0
  N24: U1.RS, LCM1602_IIC1.RS
  N25: U1.R_W, LCM1602_IIC1.RW
  N26: U1.E, LCM1602_IIC1.E
  N27: U1.DB0, LCM1602_IIC1.D0
  N28: U1.DB1, LCM1602_IIC1.D1
  N29: U1.DB2, LCM1602_IIC1.D2
  N30: U1.DB3, LCM1602_IIC1.D3
  N31: U1.DB4, LCM1602_IIC1.D4
  N32: U1.DB5, LCM1602_IIC1.D5
  N33: U1.DB6, LCM1602_IIC1.D6
  N34: U1.DB7, LCM1602_IIC1.D7
  N35: U1.A, LCM1602_IIC1.A
  N36: U1.K, LCM1602_IIC1.K

custom parts:
  TP4056 Module: TP4056 Lithium Battery Charge Management Module Links: TP4056 website
  MT3608 Module: MT3608 Boost Converter Module Links: Aerosemi MT3608 2A Step Up Converter datasheet
  18650 battery holder: 18650 Battery Holder
  LCM1602 IIC: I2C-Module to use a 1602 or 2004 LCD on with the wire.h libory Serial LCD Modul
  sensor_biometrico: Adafruit Optical Fingerprint Sensor
